// Logisim project cpu.circ as structural Verilog: 6 circuits, main circuit cpu
module cpu (
  input  clk,
  input  ram_end,
  input  [31:0] ram_data,
  output [31:0] ram_read_addr,
  output cpu_end
);

  wire beq, bgtz, blez, bltz, bneq, data_path_1_p12, data_path_1_p14, data_path_1_p15, data_path_1_p19,
       \end , eq, greater, halt, hypothesis, immediate, is_comparission, is_copy, is_jump, J, JR, less,
       not_1_out, not_2_out, or_2_out, rw, SHi, SLo, zero;
  wire [1:0] data_selector;
  wire [2:0] hypothesis_jump_selector_1_s0;
  wire [3:0] alu_selector;
  wire [4:0] DA, register_d, register_s, register_t;
  wire [5:0] func_code, op_code;
  wire [15:0] multiplexer_1_out, offset;
  wire [25:0] jump;
  wire [31:0] A, B, \const , const2, constant, constant_2, Hi, Lo, multiplexer_2_out, multiplexer_3_out,
       multiplexer_5_out, pc_next, ram;

  Multiplexer #(.width(16)) multiplexer_1 (
    .in0({16{1'b0}}), .in1(offset), .out(multiplexer_1_out), .sel(hypothesis));  // open: en
  not not_1 (not_1_out, halt);
  Multiplexer #(.width(32)) multiplexer_2 (
    .in0({32{1'b0}}), .in1(32'h1), .out(multiplexer_2_out), .sel(greater));  // open: en
  Multiplexer #(.width(32)) multiplexer_3 (
    .in0({32{1'b0}}), .in1(32'h1), .out(multiplexer_3_out), .sel(greater));  // open: en
  Register #(.width(32)) PC (.D(pc_next), .en(\end ), .Q(ram_read_addr), .clk(clk));  // open: clr
  and and_1 (\end , ram_end, not_1_out);
  Multiplexer #(.width(5)) multiplexer_4 (.in0(register_d), .in1(register_t), .out(DA), .sel(immediate));  // open: en
  Multiplexer #(.width(32)) multiplexer_5 (
    .in0(multiplexer_2_out), .in1(multiplexer_3_out), .out(multiplexer_5_out), .sel(immediate));  // open: en
  branch_control branch_control_1 (
    .PC_in(ram_read_addr), .jump(is_jump), .flag(hypothesis), .offset(multiplexer_1_out), .PC_out(pc_next),
    .J(J), .JR(JR), .constant(jump), .R_s(A));
  D_Flip_Flop d_ff_1 (.clk(clk), .D(\end ), .Q(cpu_end));  // open: Qn, preset, en, reset
  Multiplexer #(.width(32)) multiplexer_6 (
    .in0(constant), .in1(multiplexer_5_out), .out(const2), .sel(is_comparission));  // open: en
  Multiplexer #(.width(32)) multiplexer_7 (.in0(\const ), .in1({32{1'b0}}), .out(constant), .sel(zero));  // open: en
  // instruction_decoder instruction_decoder_1: pin names not known; wires that end beside it: ram_data, op_code, register_s, register_t, register_d, func_code, \const , jump, alu_selector, immediate, data_selector, rw, halt, is_comparission, is_jump, is_copy, offset
  Hi_Lo hi_lo_1 (
    .OP0(op_code[0]), .OP1(op_code[1]), .OP2(op_code[2]), .OP3(op_code[3]), .OP4(op_code[4]),
    .OP5(op_code[5]), .F0(func_code[0]), .F1(func_code[1]), .F2(func_code[2]), .F3(func_code[3]),
    .F4(func_code[4]), .F5(func_code[5]), .SHi(SHi), .SLo(SLo));
  // data_path data_path_1: pin names not known; wires that end beside it: register_s, register_t, DA, constant_2, constant, ram, rw, \end , alu_selector, data_selector, A, data_path_1_p12, B, data_path_1_p14, data_path_1_p15, greater, eq, less, data_path_1_p19
  or or_1 (data_path_1_p12, immediate, is_copy, zero);
  Multiplexer #(.select(2), .width(32)) multiplexer_8 (
    .in0(const2), .in1(Hi), .in2(Lo), .out(constant_2), .sel({SLo, SHi}));  // open: in3, en
  Register #(.width(32)) u_Hi (.Q(Hi), .clk(clk));  // open: D, en, clr
  Register #(.width(32)) u_Lo (.Q(Lo), .clk(clk));  // open: D, en, clr
  Multiplexer multiplexer_9 (.in0(1'b0), .in1(1'b1), .out(beq), .sel(eq));  // open: en
  Multiplexer multiplexer_10 (.in0(1'b0), .in1(1'b1), .out(bneq), .sel(not_2_out));  // open: en
  not not_2 (not_2_out, eq);
  Multiplexer multiplexer_11 (.in0(1'b0), .in1(1'b1), .out(blez), .sel(or_2_out));  // open: en
  or or_2 (or_2_out, greater, eq);
  Multiplexer multiplexer_12 (.in0(1'b0), .in1(1'b1), .out(bgtz), .sel(less));  // open: en
  Multiplexer multiplexer_13 (.in0(1'b0), .in1(1'b1), .out(bltz), .sel(greater));  // open: en
  hypothesis_jump_selector hypothesis_jump_selector_1 (
    .Op0(op_code[0]), .Op1(op_code[1]), .Op2(op_code[2]), .Op3(op_code[3]), .Op4(op_code[4]),
    .Op5(op_code[5]), .F0(func_code[0]), .F1(func_code[1]), .F2(func_code[2]), .F3(func_code[3]),
    .F4(func_code[4]), .F5(func_code[5]), .S0(hypothesis_jump_selector_1_s0[0]),
    .S1(hypothesis_jump_selector_1_s0[1]), .S2(hypothesis_jump_selector_1_s0[2]), .ZERO(zero), .J(J), .Jr(JR));
  Multiplexer #(.select(3)) multiplexer_14 (
    .in0(beq), .in1(bneq), .in2(blez), .in3(bgtz), .in4(bltz), .out(hypothesis),
    .sel(hypothesis_jump_selector_1_s0));  // open: in5, in6, in7, en

  // Other names for the same wires on the sheet: instruction[31:0] = ram_data; pc_current[31:0] = ram_read_addr

  // Notes on the sheet:
  //   D.ADDRESS
  //   COMPARISSIONS
  //   COPY FROM Hi/Lo
  //   JUMPS
endmodule

module cpu_test (
);

  wire clock_1_out, \end , fake_ram_1_end;
  wire [31:0] addr, fake_ram_1_data;

  fake_ram fake_ram_1 (
    .cycles(4'b0011), .clk(clock_1_out), .db0(32'h1), .db1(32'h2), .db2(32'h3), .db3(32'h4), .ad(addr),
    .data(fake_ram_1_data), .\end (fake_ram_1_end), .cpu_end(\end ));  // open: real_addr
  // Probe on fake_ram_1_data
  Clock clock_1 (.out(clock_1_out));
  cpu cpu_1 (
    .ram_end(fake_ram_1_end), .ram_data(fake_ram_1_data), .ram_read_addr(addr), .clk(clock_1_out),
    .cpu_end(\end ));
  // Probe on addr
endmodule

module fake_ram (
  input  [3:0] cycles,
  input  clk,
  input  [31:0] db0,
  input  cpu_end,
  input  [31:0] db1,
  input  [31:0] db2,
  input  [31:0] db3,
  input  [31:0] ad,
  output [31:0] data,
  output \end ,
  output [15:0] real_addr
);

  wire [1:0] db_flag;
  wire [31:0] blocks;
  wire [31:2] divider_2_out;
  wire [31:16] arddr;

  Divider #(.width(32)) divider_1 (.a(ad), .b(32'h10), .out({arddr, real_addr}), .rem(blocks));  // open: upper
  Multiplexer #(.select(2), .width(32), .enable("false")) multiplexer_1 (
    .in0(db0), .in1(db1), .in2(db2), .in3(db3), .out(data), .sel(db_flag));
  Divider #(.width(32)) divider_2 (.a(blocks), .b(32'h4), .out({divider_2_out, db_flag}));  // open: upper, rem
  waita waita_1 (.cycles(cycles), .clk(clk), .cpu_end(cpu_end), .\end (\end ));

  // Other names for the same wires on the sheet: arddr[15:0] = real_addr; real_arddr[15:0] = real_addr
endmodule

module waita (
  input  clk,
  input  [3:0] cycles,
  input  cpu_end,
  output \end 
);

  wire not_1_out;
  wire [3:0] counter_1_q;

  Counter #(.width(4), .max('hf)) counter_1 (
    .count(not_1_out), .Q(counter_1_q), .clk(clk), .clr(cpu_end));  // open: load, D, carry
  not not_1 (not_1_out, \end );
  Comparator #(.width(4)) comparator_1 (.a(counter_1_q), .b(cycles), .eq(\end ));  // open: gt, lt
endmodule

module hypothesis_jump_selector (
  input  Op0,
  input  Op1,
  input  Op2,
  input  Op3,
  input  Op4,
  input  Op5,
  input  F0,
  input  F1,
  input  F2,
  input  F3,
  input  F4,
  input  F5,
  output S0,
  output S1,
  output S2,
  output ZERO,
  output J,
  output Jr
);

  wire and_4_out, and_5_out, not_1_out, not_2_out, not_3_out, not_4_out, not_5_out, not_6_out, not_7_out,
       not_8_out, not_9_out, not_10_out, not_11_out, not_12_out, not_13_out, not_14_out, not_15_out,
       not_16_out, not_17_out, not_18_out, not_19_out, not_20_out, not_21_out, not_22_out, not_23_out,
       not_24_out, not_25_out, not_26_out, not_27_out, not_28_out, not_29_out, not_30_out, not_31_out,
       not_32_out, not_33_out, not_34_out, not_35_out;

  not not_1 (not_1_out, Op1);
  not not_2 (not_2_out, Op2);
  not not_3 (not_3_out, Op3);
  not not_4 (not_4_out, Op4);
  not not_5 (not_5_out, Op5);
  not not_6 (not_6_out, Op3);
  not not_7 (not_7_out, Op4);
  not not_8 (not_8_out, Op5);
  not not_9 (not_9_out, Op3);
  not not_10 (not_10_out, Op4);
  not not_11 (not_11_out, Op5);
  not not_12 (not_12_out, Op3);
  not not_13 (not_13_out, Op4);
  not not_14 (not_14_out, Op5);
  not not_15 (not_15_out, Op1);
  not not_16 (not_16_out, Op2);
  not not_17 (not_17_out, Op3);
  not not_18 (not_18_out, Op4);
  not not_19 (not_19_out, Op5);
  not not_20 (not_20_out, Op0);
  not not_21 (not_21_out, Op2);
  not not_22 (not_22_out, Op3);
  not not_23 (not_23_out, Op4);
  not not_24 (not_24_out, Op5);
  not not_25 (not_25_out, Op0);
  not not_26 (not_26_out, Op1);
  not not_27 (not_27_out, Op2);
  not not_28 (not_28_out, Op3);
  not not_29 (not_29_out, Op4);
  not not_30 (not_30_out, Op5);
  not not_31 (not_31_out, F0);
  not not_32 (not_32_out, F1);
  not not_33 (not_33_out, F2);
  not not_34 (not_34_out, F4);
  not not_35 (not_35_out, F5);
  and and_1 (S0, Op0, not_1_out, not_2_out, not_3_out, not_4_out, not_5_out);
  and and_2 (S1, Op1, Op2, not_6_out, not_7_out, not_8_out);
  and and_3 (S2, Op0, Op2, not_9_out, not_10_out, not_11_out);
  and and_4 (and_4_out, Op1, Op2, not_12_out, not_13_out, not_14_out);
  and and_5 (and_5_out, Op0, not_15_out, not_16_out, not_17_out, not_18_out, not_19_out);
  and and_6 (J, not_20_out, Op1, not_21_out, not_22_out, not_23_out, not_24_out);
  and and_7 (Jr, not_25_out, not_26_out, not_27_out, not_28_out, not_29_out, not_30_out, not_31_out, not_32_out, not_33_out, F3, not_34_out, not_35_out);
  or or_1 (ZERO, and_4_out, and_5_out);
endmodule

module Hi_Lo (
  input  OP0,
  input  OP1,
  input  OP2,
  input  OP3,
  input  OP4,
  input  OP5,
  input  F0,
  input  F1,
  input  F2,
  input  F3,
  input  F4,
  input  F5,
  output SHi,
  output SLo
);

  wire not_1_out, not_2_out, not_3_out, not_4_out, not_5_out, not_6_out, not_7_out, not_8_out, not_9_out,
       not_10_out, not_11_out, not_12_out, not_13_out, not_14_out, not_15_out, not_16_out, not_17_out,
       not_18_out, not_19_out, not_20_out, not_21_out;

  not not_1 (not_1_out, OP0);
  not not_2 (not_2_out, OP1);
  not not_3 (not_3_out, OP2);
  not not_4 (not_4_out, OP3);
  not not_5 (not_5_out, OP4);
  not not_6 (not_6_out, OP5);
  not not_7 (not_7_out, F0);
  not not_8 (not_8_out, F1);
  not not_9 (not_9_out, F2);
  not not_10 (not_10_out, F3);
  not not_11 (not_11_out, F5);
  not not_12 (not_12_out, OP0);
  not not_13 (not_13_out, OP1);
  not not_14 (not_14_out, OP2);
  not not_15 (not_15_out, OP3);
  not not_16 (not_16_out, OP4);
  not not_17 (not_17_out, OP5);
  not not_18 (not_18_out, F0);
  not not_19 (not_19_out, F2);
  not not_20 (not_20_out, F3);
  not not_21 (not_21_out, F5);
  and and_1 (SHi, not_1_out, not_2_out, not_3_out, not_4_out, not_5_out, not_6_out, not_7_out, not_8_out, not_9_out, not_10_out, F4, not_11_out);
  and and_2 (SLo, not_12_out, not_13_out, not_14_out, not_15_out, not_16_out, not_17_out, not_18_out, F1, not_19_out, not_20_out, F4, not_21_out);
endmodule
